# Fritzing sketch sfeer licht (saved by Fritzing 0.9.3b)
breadboards: 1

parts:
  Part2 = Arduino Uno (Rev3)
  R4 = Resistor [tolerance=±5% resistance=300 package=THT]
  J2 = female pin header, 3 pins [form="♀ (female)"]
  R5 = Trimmer Potentiometer [maximum_resistance=10kΩ package=THT]
  R7 = Resistor [tolerance=±5% resistance=220 package=THT]
  R9 = Resistor [tolerance=±5% resistance=220 package=THT]
  R8 = Temperature Sensor (Thermistor) [thermistor_type=NTC package=THT]
  R6 = Photocell (LDR) [package=THT]

nets:
  N1: Part2.A3, R9.Pin_1, R8.pin_0
  N2: Part2.A4/SDA, R7.Pin_1, R6.pin_0
  N3: Part2.A5/SCL, R5.wiper
  N4: Part2.D9_PWM, R4.Pin_1
  N5: Part2.5V, J2.pin1, R5.leg2, R7.Pin_0, R9.Pin_0
  N6: Part2.GND, J2.pin3, R5.leg1, R8.pin_1
  N7: R4.Pin_0, J2.pin2

notes:
  sfeer licht
  let op de draad kleuren van de smart-leds!!!
